// Logisim project CIRCUITOS.circ as structural Verilog: 3 circuits, main circuit main
module main (
);

  B__AC b_ac_1 ();  // open: out_4, A, B, C
  B_A b_a_1 ();  // open: out_3, A, B
endmodule

module B__AC (
  input  A,
  input  B,
  input  C,
  output out_4
);

  wire and_1_out;

  and and_1 (and_1_out, A, C);
  or or_1 (out_4, and_1_out, ~B);  // OR_Gate
endmodule

module B_A (
  input  A,
  input  B,
  output out_3
);

  or or_1 (out_3, B, A);
endmodule
